# Fritzing sketch picowsolar (saved by Fritzing 0.9.9b)

parts:
  Mod1 = Raspberry Pi Pico
  D1 = SOLAR-IXYS [package=solarbit-12x1]
  D2 = SOLAR-IXYS [package=solarbit-12x1]
  TP1 = TP4056 [chip_label=TP4056 package="DIP (Dual Inline) [THT]"]
  Capacitive_Soil_Moisture_Sensor1 = DFRobot Capacitive Soil Moisture Sensor V1.0 [part_number=SEN0193]
  DS1 = DS18B20 1-Wire Temperature Sensor [part_number=DS18B20]
  R1 = Resistor [tolerance=±5% resistance=470k package="2512 [SMD]"]  # not connected
  R2 = Resistor [tolerance=±5% resistance=1M package="0603 [SMD]"]
  C1 = Ceramic Capacitor [capacitance=100nF voltage=35V package="200 mil [THT, multilayer]"]
  C2 = Ceramic Capacitor [capacitance=100nF voltage=35V package="200 mil [THT, multilayer]"]
  U1 = LIPO-1000mAh [package=lipo-1000]
  S1 = Momentary Switch [package=ksa_sealed_tac_switch]
  S2 = Momentary Switch [package=ksa_sealed_tac_switch]

nets:
  GND: Mod1.pin_3, Mod1.pin_23, Mod1.pin_28, Mod1.pin_33, Mod1.pin_38, Mod1.pin_42, TP1.pin6, Capacitive_Soil_Moisture_Sensor1.GND, DS1.GND, C1.1, C2.1, S1.2, S2.2
  N1: Mod1.pin_4, DS1.DQ
  N2: Mod1.pin_25, S2.4
  N3: Mod1.pin_29, Capacitive_Soil_Moisture_Sensor1.VCC
  N4: Mod1.pin_30, S1.4
  N5: Mod1.pin_31, Capacitive_Soil_Moisture_Sensor1.A
  N6: Mod1.pin_32, R2.Pin_0
  N7: Mod1.pin_35, C2.0
  N8: Mod1.pin_36, DS1.VDD
  N9: Mod1.pin_39, TP1.pin3, C1.0
  N10: D1.A, D2.C
  N11: D1.C, R2.Pin_1
  N12: D2.A, TP1.pin2
  N13: TP1.pin4, U1.+
  N14: TP1.pin5, U1.-

custom parts:
  Raspberry Pi Pico: Raspberry Pi Pico. Based around the RP2040 microcontroller the Pico is a low cost microcontroller device bringing Raspberry Pi quality, cost, and easy of use to the microcontroller space. Jan 2021, Split part in to two versions: tht (this one) and SMD. This one will drill holes for a .1 in header in pcb to allow plugging in the module as well as providing pads to solder the module to the top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
  TP4056: A DIP stand-in part for whatever IC you want. With 6 pins on a 300mil dual inline package (DIP) footprint.
  DFRobot Capacitive Soil Moisture Sensor V1.0: DFRobot Capacitive Soil Moisture Sensor V1.0 This product measures soil moisture levels by capacitive sensing, rather than resistive sensing like other types of moisture sensor. It is made of a corrosion resistant material giving it a long service life. Insert it into soil and impress your friends with the real-time soil moisture data! The product includes an on-board voltage regulator which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
